# Fritzing sketch SciFiAnalyser (saved by Fritzing 0.9.4)

parts:
  C1 = Electrolytic Capacitor [capacitance=1µF package="100 mil [THT, electrolytic]"]
  Part1 = Arduino Nano (Rev3.0)
  S1 = Toggle Switch [part_number="Toggle Switch" package=THT]
  R2 = Slide Potentiometer [maximum_resistance=100kΩ]
  U1 = LCD-16X2 [package=lcd-16x2_noholes]
  Part3 = 24 NeoPixel Ring [part_number=1586]
  R3 = Resistor [tolerance=±5% resistance=330 package=THT]
  BATT2 = 4xAA Switchable Battery Pack w/Bare Wire
  BUTTON1 = Arcade Button (green)
  J1 = Piezo Speaker

nets:
  GND: C1.-, Part1.GND, R2.leg2, U1.K, Part3.GND, BATT2.NEG, BUTTON1.no_name_yet#1, J1.pin1
  5V: C1.+, Part1.5V, R2.leg1, U1.A, Part3.VDD
  N1: Part1.D2, R3.Pin_1
  N2: Part1.D4, J1.pin2
  N3: Part1.VIN, S1.L2
  N4: Part1.A7, R2.wiper
  N5: Part1.A5, U1.DB7
  N6: Part1.A4, U1.DB6
  N7: Part1.A2, BUTTON1.no_name_yet#2
  N8: S1.COM, BATT2.POS
  N9: Part3.IN, R3.Pin_0

notes:
  AA battery pack
  -ve -> Arduino GND
  +ve -> Switch -> Arduino VIn
  LCD display with I2C backpack
  VCC -> Arduino 5V
  GND -> GND
  SDA -> Arduino A4
  SCL -> Arduino A5
  Arcade button wired to Arduino pin A2 and GND
  Buzzer wired to Arduino pin 4 and GND
  Linear slide potentiometer wired to Arduino 5V, GND, and A7
  WS2812B ("Neopixel") ring wired to 5V, GND, and Arduino Pin 2 (via 330Ω resistor)

custom parts:
  Toggle Switch: A "missile"-style toggle switch with LED tip, e.g. https://www.sparkfun.com/products/11310
  24 NeoPixel Ring: 24 ultra bright smart LED NeoPixels are arranged in a circle with 2.6" (66mm) outer diameter. The rings are 'chainable' - connect the output pin of one to the input pin of another. Use only one microcontroller pin to control as many as you can chain together! Each LED is addressable as the driver chip is inside the LED. Each one has ~18mA constant current drive so the color will be very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
  4xAA Switchable Battery Pack w/Bare Wire: 4xAA Switchable Battery Pack with Bare Wire connection
  Arcade Button (green): Adafruit Arcade Button (green)
